# Fritzing sketch serial-thing (saved by Fritzing 1.0.4)
breadboards: 1

parts:
  M1 = Arduino NANO RP2040 CONNECT with headers
  R1 = Resistor [tolerance=±5% resistance=10k package="2512 [SMD]"]
  R2 = Resistor [tolerance=±5% resistance=10k package="2512 [SMD]"]
  R3 = Resistor [tolerance=±5% resistance=10k package="2512 [SMD]"]
  R4 = Resistor [tolerance=±5% resistance=10k package="2512 [SMD]"]
  R5 = Resistor [tolerance=±5% resistance=10k package="2512 [SMD]"]
  R6 = Resistor [tolerance=±5% resistance=10k package="2512 [SMD]"]

nets:
  N1: M1.GND-4, M1.GND-29, R5.Pin_0
  N2: M1.D17, R3.Pin_1, R4.Pin_1, R6.Pin_0
  N3: M1.D20, R1.Pin_1, R2.Pin_1, R5.Pin_1
  N4: R1.Pin_0, R2.Pin_0
  N5: R3.Pin_0, R4.Pin_0
